// Logisim project stage6B.circ as structural Verilog: 5 circuits, main circuit main
module main (
);

  wire and_1_out, and_2_out, and_3_out, and_4_out, and_5_out, and_6_out, and_7_out, and_8_out, and_9_out,
       and_10_out, and_11_out, and_12_out, and_13_out, and_14_out, and_15_out, button_1_out, button_2_out,
       button_3_out, clock_1_out, j_k_ff_1_q, j_k_ff_2_q, j_k_ff_3_q, j_k_ff_4_q, j_k_ff_5_q, j_k_ff_6_q,
       j_k_ff_7_q, j_k_ff_8_q, j_k_ff_9_q, j_k_ff_10_q, j_k_ff_11_q, j_k_ff_12_q, j_k_ff_13_q, j_k_ff_14_q,
       j_k_ff_15_q, not_1_out, not_2_out, or_1_out, or_2_out, or_3_out, or_4_out, t_ff_1_q;
  wire [2:0] counterz_1_count, d_ff_4_q;
  wire [3:0] d_ff_1_q, d_ff_2_q, d_ff_3_q, show_split_1_out_7, show_split_2_out_7, show_split_3_out_7,
       show_split_4_out_7, split_record_1_out_18, split_record_1_out_19, split_record_1_out_20,
       split_record_1_out_21, split_record_2_out_18, split_record_2_out_19, split_record_2_out_20,
       split_record_2_out_21, split_record_3_out_18, split_record_3_out_19, split_record_3_out_20,
       split_record_3_out_21, split_record_4_out_18, split_record_4_out_19, split_record_4_out_20,
       split_record_4_out_21, split_record_5_out_18, split_record_5_out_19, split_record_5_out_20,
       split_record_5_out_21;

  Hex_Digit_Display hex_digit_display_1 (.value(d_ff_3_q));  // open: dp
  Hex_Digit_Display hex_digit_display_2 (.value(d_ff_2_q));  // open: dp
  Button button_1 (.out(button_1_out));
  Hex_Digit_Display hex_digit_display_3 (.value({1'b0, d_ff_4_q}));  // open: dp
  Hex_Digit_Display hex_digit_display_4 (.value(d_ff_1_q));  // open: dp
  Button button_2 (.out(button_2_out));
  Button button_3 (.out(button_3_out));
  Hex_Digit_Display hex_digit_display_5 (.value(show_split_4_out_7));  // open: dp
  Hex_Digit_Display hex_digit_display_6 (.value(show_split_3_out_7));  // open: dp
  LED led_1 (.in(t_ff_1_q));
  Hex_Digit_Display hex_digit_display_7 (.value(show_split_2_out_7));  // open: dp
  T_Flip_Flop t_ff_1 (.T(1'b1), .clk(button_1_out), .Q(t_ff_1_q), .reset(button_3_out));  // open: Qn, preset
  Hex_Digit_Display hex_digit_display_8 (.value(show_split_1_out_7));  // open: dp
  Clock clock_1 (.out(clock_1_out));
  J_K_Flip_Flop j_k_ff_1 (
    .J(t_ff_1_q), .K(t_ff_1_q), .clk(clock_1_out), .Q(j_k_ff_1_q), .reset(or_1_out));  // open: Qn, preset
  J_K_Flip_Flop j_k_ff_2 (
    .J(t_ff_1_q), .K(t_ff_1_q), .clk(or_2_out), .Q(j_k_ff_2_q), .reset(or_3_out));  // open: Qn, preset
  J_K_Flip_Flop j_k_ff_3 (.J(1'b1), .K(1'b1), .clk(or_3_out), .Q(j_k_ff_3_q), .reset(or_4_out));  // open: Qn, preset
  and and_1 (and_1_out, t_ff_1_q, j_k_ff_1_q);
  D_Flip_Flop #(.trigger("falling")) d_ff_1 (
    .D(j_k_ff_1_q), .clk(clock_1_out), .Q(d_ff_1_q[0]), .reset(button_3_out));  // open: Qn, preset
  J_K_Flip_Flop j_k_ff_4 (.J(1'b1), .K(1'b1), .clk(or_1_out), .Q(j_k_ff_4_q), .reset(or_2_out));  // open: Qn, preset
  and and_2 (and_2_out, t_ff_1_q, j_k_ff_2_q);
  D_Flip_Flop #(.trigger("falling")) d_ff_2 (
    .D(j_k_ff_2_q), .clk(clock_1_out), .Q(d_ff_2_q[0]), .reset(button_3_out));  // open: Qn, preset
  D_Flip_Flop #(.trigger("falling")) d_ff_3 (
    .D(j_k_ff_3_q), .clk(clock_1_out), .Q(d_ff_3_q[0]), .reset(button_3_out));  // open: Qn, preset
  J_K_Flip_Flop j_k_ff_5 (
    .J(and_1_out), .K(and_1_out), .clk(clock_1_out), .Q(j_k_ff_5_q), .reset(or_1_out));  // open: Qn, preset
  D_Flip_Flop #(.trigger("falling")) d_ff_4 (
    .D(j_k_ff_4_q), .clk(clock_1_out), .Q(d_ff_4_q[0]), .reset(button_3_out));  // open: Qn, preset
  J_K_Flip_Flop j_k_ff_6 (
    .J(and_2_out), .K(and_2_out), .clk(or_2_out), .Q(j_k_ff_6_q), .reset(or_3_out));  // open: Qn, preset
  J_K_Flip_Flop j_k_ff_7 (
    .J(j_k_ff_3_q), .K(j_k_ff_3_q), .clk(or_3_out), .Q(j_k_ff_7_q), .reset(or_4_out));  // open: Qn, preset
  and and_3 (and_3_out, and_1_out, j_k_ff_5_q);
  D_Flip_Flop #(.trigger("falling")) d_ff_5 (
    .D(j_k_ff_5_q), .clk(clock_1_out), .Q(d_ff_1_q[1]), .reset(button_3_out));  // open: Qn, preset
  J_K_Flip_Flop j_k_ff_8 (
    .J(j_k_ff_4_q), .K(j_k_ff_4_q), .clk(or_1_out), .Q(j_k_ff_8_q), .reset(or_2_out));  // open: Qn, preset
  and and_4 (and_4_out, and_2_out, j_k_ff_6_q);
  D_Flip_Flop #(.trigger("falling")) d_ff_6 (
    .D(j_k_ff_6_q), .clk(clock_1_out), .Q(d_ff_2_q[1]), .reset(button_3_out));  // open: Qn, preset
  and and_5 (and_5_out, j_k_ff_3_q, j_k_ff_7_q);
  D_Flip_Flop #(.trigger("falling")) d_ff_7 (
    .D(j_k_ff_7_q), .clk(clock_1_out), .Q(d_ff_3_q[1]), .reset(button_3_out));  // open: Qn, preset
  J_K_Flip_Flop j_k_ff_9 (
    .J(and_3_out), .K(and_3_out), .clk(clock_1_out), .Q(j_k_ff_9_q), .reset(or_1_out));  // open: Qn, preset
  and and_6 (and_6_out, j_k_ff_4_q, j_k_ff_8_q);
  D_Flip_Flop #(.trigger("falling")) d_ff_8 (
    .D(j_k_ff_8_q), .clk(clock_1_out), .Q(d_ff_4_q[1]), .reset(button_3_out));  // open: Qn, preset
  J_K_Flip_Flop j_k_ff_10 (
    .J(and_4_out), .K(and_4_out), .clk(or_2_out), .Q(j_k_ff_10_q), .reset(or_3_out));  // open: Qn, preset
  J_K_Flip_Flop j_k_ff_11 (
    .J(and_5_out), .K(and_5_out), .clk(or_3_out), .Q(j_k_ff_11_q), .reset(or_4_out));  // open: Qn, preset
  and and_7 (and_7_out, and_3_out, j_k_ff_9_q);
  D_Flip_Flop #(.trigger("falling")) d_ff_9 (
    .D(j_k_ff_9_q), .clk(clock_1_out), .Q(d_ff_1_q[2]), .reset(button_3_out));  // open: Qn, preset
  J_K_Flip_Flop j_k_ff_12 (
    .J(and_6_out), .K(and_6_out), .clk(or_1_out), .Q(j_k_ff_12_q), .reset(or_2_out));  // open: Qn, preset
  and and_8 (and_8_out, and_4_out, j_k_ff_10_q);
  D_Flip_Flop #(.trigger("falling")) d_ff_10 (
    .D(j_k_ff_10_q), .clk(clock_1_out), .Q(d_ff_2_q[2]), .reset(button_3_out));  // open: Qn, preset
  and and_9 (and_9_out, and_5_out, j_k_ff_11_q);
  D_Flip_Flop #(.trigger("falling")) d_ff_11 (
    .D(j_k_ff_11_q), .clk(clock_1_out), .Q(d_ff_3_q[2]), .reset(button_3_out));  // open: Qn, preset
  not not_1 (not_1_out, t_ff_1_q);
  J_K_Flip_Flop j_k_ff_13 (
    .J(and_7_out), .K(and_7_out), .clk(clock_1_out), .Q(j_k_ff_13_q), .reset(or_1_out));  // open: Qn, preset
  and and_10 (and_10_out, j_k_ff_8_q, j_k_ff_12_q);
  D_Flip_Flop #(.trigger("falling")) d_ff_12 (
    .D(j_k_ff_12_q), .clk(clock_1_out), .Q(d_ff_4_q[2]), .reset(button_3_out));  // open: Qn, preset
  J_K_Flip_Flop j_k_ff_14 (
    .J(and_8_out), .K(and_8_out), .clk(or_2_out), .Q(j_k_ff_14_q), .reset(or_3_out));  // open: Qn, preset
  J_K_Flip_Flop j_k_ff_15 (
    .J(and_9_out), .K(and_9_out), .clk(or_3_out), .Q(j_k_ff_15_q), .reset(or_4_out));  // open: Qn, preset
  and and_11 (and_11_out, t_ff_1_q, button_2_out);
  and and_12 (and_12_out, j_k_ff_5_q, j_k_ff_13_q);
  D_Flip_Flop #(.trigger("falling")) d_ff_13 (
    .D(j_k_ff_13_q), .clk(clock_1_out), .Q(d_ff_1_q[3]), .reset(button_3_out));  // open: Qn, preset
  and and_13 (and_13_out, j_k_ff_6_q, j_k_ff_14_q);
  D_Flip_Flop #(.trigger("falling")) d_ff_14 (
    .D(j_k_ff_14_q), .clk(clock_1_out), .Q(d_ff_2_q[3]), .reset(button_3_out));  // open: Qn, preset
  and and_14 (and_14_out, j_k_ff_7_q, j_k_ff_15_q);
  D_Flip_Flop #(.trigger("falling")) d_ff_15 (
    .D(j_k_ff_15_q), .clk(clock_1_out), .Q(d_ff_3_q[3]), .reset(button_3_out));  // open: Qn, preset
  and and_15 (and_15_out, not_1_out, button_2_out);
  or or_1 (or_1_out, and_12_out, button_3_out);
  or or_2 (or_2_out, and_10_out, button_3_out);
  or or_3 (or_3_out, and_13_out, button_3_out);
  or or_4 (or_4_out, and_14_out, button_3_out);
  not not_2 (not_2_out, t_ff_1_q);
  counterz counterz_1 (.power(not_2_out), .split(and_15_out), .count(counterz_1_count));
  show_split show_split_1 (
    .Cin(counterz_1_count), .fourth(split_record_4_out_21), .fifth(split_record_5_out_21),
    .first(split_record_1_out_21), .second(split_record_2_out_21), .third(split_record_3_out_21),
    .out_7(show_split_1_out_7));
  show_split show_split_2 (
    .Cin(counterz_1_count), .fourth(split_record_4_out_20), .fifth(split_record_5_out_20),
    .first(split_record_1_out_20), .second(split_record_2_out_20), .third(split_record_3_out_20),
    .out_7(show_split_2_out_7));
  show_split show_split_3 (
    .Cin(counterz_1_count), .fourth(split_record_4_out_19), .fifth(split_record_5_out_19),
    .first(split_record_1_out_19), .second(split_record_2_out_19), .third(split_record_3_out_19),
    .out_7(show_split_3_out_7));
  show_split show_split_4 (
    .Cin(counterz_1_count), .fourth(split_record_4_out_18), .fifth(split_record_5_out_18),
    .first(split_record_1_out_18), .second(split_record_2_out_18), .third(split_record_3_out_18),
    .out_7(show_split_4_out_7));
  Hex_Digit_Display Counter (.value({1'b0, counterz_1_count}));  // open: dp
  split_record split_record_1 (
    .split(and_11_out), .reset(button_3_out), .secondOnes(d_ff_1_q[0]), .secondOnes2(d_ff_1_q[1]),
    .secondOnes3(d_ff_1_q[2]), .secondOnes4(d_ff_1_q[3]), .secondTens(d_ff_4_q[0]),
    .secondTens2(d_ff_4_q[1]), .secondTens3(d_ff_4_q[2]), .minuteOnes(d_ff_2_q[0]),
    .minuteOnes2(d_ff_2_q[1]), .minuteOnes3(d_ff_2_q[2]), .minuteOnes4(d_ff_2_q[3]),
    .minuteTens(d_ff_3_q[0]), .minuteTens2(d_ff_3_q[1]), .minuteTens3(d_ff_3_q[2]),
    .minuteTens4(d_ff_3_q[3]), .out_18(split_record_1_out_18), .out_19(split_record_1_out_19),
    .out_20(split_record_1_out_20), .out_21(split_record_1_out_21));
  Hex_Digit_Display hex_digit_display_9 (.value(split_record_2_out_18));  // open: dp
  split_record split_record_2 (
    .split(and_11_out), .reset(button_3_out), .secondOnes(split_record_1_out_21[0]),
    .secondOnes2(split_record_1_out_21[1]), .secondOnes3(split_record_1_out_21[2]),
    .secondOnes4(split_record_1_out_21[3]), .secondTens(split_record_1_out_20[0]),
    .secondTens2(split_record_1_out_20[1]), .secondTens3(split_record_1_out_20[2]),
    .minuteOnes(split_record_1_out_19[0]), .minuteOnes2(split_record_1_out_19[1]),
    .minuteOnes3(split_record_1_out_19[2]), .minuteOnes4(split_record_1_out_19[3]),
    .minuteTens(split_record_1_out_18[0]), .minuteTens2(split_record_1_out_18[1]),
    .minuteTens3(split_record_1_out_18[2]), .minuteTens4(split_record_1_out_18[3]),
    .out_18(split_record_2_out_18), .out_19(split_record_2_out_19), .out_20(split_record_2_out_20),
    .out_21(split_record_2_out_21));
  Hex_Digit_Display hex_digit_display_10 (.value(split_record_2_out_19));  // open: dp
  Hex_Digit_Display hex_digit_display_11 (.value(split_record_2_out_20));  // open: dp
  Hex_Digit_Display hex_digit_display_12 (.value(split_record_2_out_21));  // open: dp
  Hex_Digit_Display hex_digit_display_13 (.value(split_record_3_out_18));  // open: dp
  split_record split_record_3 (
    .split(and_11_out), .reset(button_3_out), .secondOnes(split_record_2_out_21[0]),
    .secondOnes2(split_record_2_out_21[1]), .secondOnes3(split_record_2_out_21[2]),
    .secondOnes4(split_record_2_out_21[3]), .secondTens(split_record_2_out_20[0]),
    .secondTens2(split_record_2_out_20[1]), .secondTens3(split_record_2_out_20[2]),
    .minuteOnes(split_record_2_out_19[0]), .minuteOnes2(split_record_2_out_19[1]),
    .minuteOnes3(split_record_2_out_19[2]), .minuteOnes4(split_record_2_out_19[3]),
    .minuteTens(split_record_2_out_18[0]), .minuteTens2(split_record_2_out_18[1]),
    .minuteTens3(split_record_2_out_18[2]), .minuteTens4(split_record_2_out_18[3]),
    .out_18(split_record_3_out_18), .out_19(split_record_3_out_19), .out_20(split_record_3_out_20),
    .out_21(split_record_3_out_21));
  Hex_Digit_Display hex_digit_display_14 (.value(split_record_3_out_19));  // open: dp
  Hex_Digit_Display hex_digit_display_15 (.value(split_record_3_out_20));  // open: dp
  Hex_Digit_Display hex_digit_display_16 (.value(split_record_3_out_21));  // open: dp
  split_record split_record_4 (
    .split(and_11_out), .reset(button_3_out), .secondOnes(split_record_3_out_21[0]),
    .secondOnes2(split_record_3_out_21[1]), .secondOnes3(split_record_3_out_21[2]),
    .secondOnes4(split_record_3_out_21[3]), .secondTens(split_record_3_out_20[0]),
    .secondTens2(split_record_3_out_20[1]), .secondTens3(split_record_3_out_20[2]),
    .minuteOnes(split_record_3_out_19[0]), .minuteOnes2(split_record_3_out_19[1]),
    .minuteOnes3(split_record_3_out_19[2]), .minuteOnes4(split_record_3_out_19[3]),
    .minuteTens(split_record_3_out_18[0]), .minuteTens2(split_record_3_out_18[1]),
    .minuteTens3(split_record_3_out_18[2]), .minuteTens4(split_record_3_out_18[3]),
    .out_18(split_record_4_out_18), .out_19(split_record_4_out_19), .out_20(split_record_4_out_20),
    .out_21(split_record_4_out_21));
  Hex_Digit_Display hex_digit_display_17 (.value(split_record_4_out_18));  // open: dp
  Hex_Digit_Display hex_digit_display_18 (.value(split_record_4_out_19));  // open: dp
  Hex_Digit_Display hex_digit_display_19 (.value(split_record_4_out_20));  // open: dp
  Hex_Digit_Display hex_digit_display_20 (.value(split_record_4_out_21));  // open: dp
  split_record split_record_5 (
    .split(and_11_out), .reset(button_3_out), .secondOnes(split_record_4_out_21[0]),
    .secondOnes2(split_record_4_out_21[1]), .secondOnes3(split_record_4_out_21[2]),
    .secondOnes4(split_record_4_out_21[3]), .secondTens(split_record_4_out_20[0]),
    .secondTens2(split_record_4_out_20[1]), .secondTens3(split_record_4_out_20[2]),
    .minuteOnes(split_record_4_out_19[0]), .minuteOnes2(split_record_4_out_19[1]),
    .minuteOnes3(split_record_4_out_19[2]), .minuteOnes4(split_record_4_out_19[3]),
    .minuteTens(split_record_4_out_18[0]), .minuteTens2(split_record_4_out_18[1]),
    .minuteTens3(split_record_4_out_18[2]), .minuteTens4(split_record_4_out_18[3]),
    .out_18(split_record_5_out_18), .out_19(split_record_5_out_19), .out_20(split_record_5_out_20),
    .out_21(split_record_5_out_21));
  Hex_Digit_Display hex_digit_display_21 (.value(split_record_5_out_18));  // open: dp
  Hex_Digit_Display hex_digit_display_22 (.value(split_record_5_out_19));  // open: dp
  Hex_Digit_Display hex_digit_display_23 (.value(split_record_5_out_20));  // open: dp
  Hex_Digit_Display hex_digit_display_24 (.value(split_record_5_out_21));  // open: dp
  // also tied to GND on the sheet: {split_record_1_out_20[3], split_record_2_out_20[3], split_record_3_out_20[3], split_record_4_out_20[3]}

  // Notes on the sheet:
  //   Elapsed Time
  //   Minutes
  //   :
  //   Start / Stop
  //   Seconds
  //   Stopwatch Interface
  //   Split
  //   Reset
  //   Minutes
  //   Clock Started
  //   Split Time
  //   :
  //   Seconds
  //   Counter needs to stay 0 to work properly
  //   Minutes
  //   Split 2
  //   :
  //   Seconds
  //   Split 3
  //   Minutes
  //   :
  //   Seconds
  //   Minutes
  //   Split 4
  //   :
  //   Seconds
  //   Minutes
  //   Split 5
  //   :
  //   Seconds
endmodule

module split_time (
  input  split,
  input  reset,
  input  in_3,
  input  in_4,
  input  in_5,
  input  in_6,
  output [3:0] out_7
);

  D_Flip_Flop d_ff_1 (.D(in_3), .clk(split), .Q(out_7[0]), .reset(reset));  // open: Qn, preset
  D_Flip_Flop d_ff_2 (.D(in_4), .clk(split), .Q(out_7[1]), .reset(reset));  // open: Qn, preset
  D_Flip_Flop d_ff_3 (.D(in_5), .clk(split), .Q(out_7[2]), .reset(reset));  // open: Qn, preset
  D_Flip_Flop d_ff_4 (.D(in_6), .clk(split), .Q(out_7[3]), .reset(reset));  // open: Qn, preset
endmodule

module split_record (
  input  split,
  input  reset,
  input  secondOnes,
  input  secondOnes2,
  input  secondOnes3,
  input  secondOnes4,
  input  secondTens,
  input  secondTens2,
  input  secondTens3,
  input  minuteOnes,
  input  minuteOnes2,
  input  minuteOnes3,
  input  minuteOnes4,
  input  minuteTens,
  input  minuteTens2,
  input  minuteTens3,
  input  minuteTens4,
  output [3:0] out_18,
  output [3:0] out_19,
  output [3:0] out_20,
  output [3:0] out_21
);

  D_Flip_Flop d_ff_1 (.D(secondOnes), .clk(split), .Q(out_21[0]), .reset(reset));  // open: Qn, preset
  D_Flip_Flop d_ff_2 (.D(minuteOnes), .clk(split), .Q(out_19[0]), .reset(reset));  // open: Qn, preset
  D_Flip_Flop d_ff_3 (.D(minuteTens), .clk(split), .Q(out_18[0]), .reset(reset));  // open: Qn, preset
  D_Flip_Flop d_ff_4 (.D(secondTens), .clk(split), .Q(out_20[0]), .reset(reset));  // open: Qn, preset
  D_Flip_Flop d_ff_5 (.D(secondOnes2), .clk(split), .Q(out_21[1]), .reset(reset));  // open: Qn, preset
  D_Flip_Flop d_ff_6 (.D(secondTens2), .clk(split), .Q(out_20[1]), .reset(reset));  // open: Qn, preset
  D_Flip_Flop d_ff_7 (.D(minuteOnes2), .clk(split), .Q(out_19[1]), .reset(reset));  // open: Qn, preset
  D_Flip_Flop d_ff_8 (.D(minuteTens2), .clk(split), .Q(out_18[1]), .reset(reset));  // open: Qn, preset
  D_Flip_Flop d_ff_9 (.D(secondOnes3), .clk(split), .Q(out_21[2]), .reset(reset));  // open: Qn, preset
  D_Flip_Flop d_ff_10 (.D(secondTens3), .clk(split), .Q(out_20[2]), .reset(reset));  // open: Qn, preset
  D_Flip_Flop d_ff_11 (.D(minuteOnes3), .clk(split), .Q(out_19[2]), .reset(reset));  // open: Qn, preset
  D_Flip_Flop d_ff_12 (.D(minuteTens3), .clk(split), .Q(out_18[2]), .reset(reset));  // open: Qn, preset
  D_Flip_Flop d_ff_13 (.D(secondOnes4), .clk(split), .Q(out_21[3]), .reset(reset));  // open: Qn, preset
  D_Flip_Flop d_ff_14 (.D(minuteOnes4), .clk(split), .Q(out_19[3]), .reset(reset));  // open: Qn, preset
  D_Flip_Flop d_ff_15 (.D(minuteTens4), .clk(split), .Q(out_18[3]), .reset(reset));  // open: Qn, preset

  assign out_20[3] = 1'b0;
endmodule

module show_split (
  input  [3:0] first,
  input  [3:0] second,
  input  [3:0] third,
  input  [3:0] fourth,
  input  [3:0] fifth,
  input  [2:0] Cin,
  output [3:0] out_7
);

  wire not_1_out, not_2_out, not_3_out;
  wire [3:0] and_1_out, and_5_out, and_9_out, and_13_out, and_17_out;

  not not_1 (not_1_out, Cin[0]);
  not not_2 (not_2_out, Cin[1]);
  not not_3 (not_3_out, Cin[2]);
  and and_1 (and_1_out[0], first[0], not_1_out, not_2_out, not_3_out);
  and and_2 (and_1_out[1], first[1], not_1_out, not_2_out, not_3_out);
  and and_3 (and_1_out[2], first[2], not_1_out, not_2_out, not_3_out);
  and and_4 (and_1_out[3], first[3], not_1_out, not_2_out, not_3_out);
  and and_5 (and_5_out[0], second[0], Cin[0], not_2_out, not_3_out);
  and and_6 (and_5_out[1], second[1], Cin[0], not_2_out, not_3_out);
  and and_7 (and_5_out[2], second[2], Cin[0], not_2_out, not_3_out);
  and and_8 (and_5_out[3], second[3], Cin[0], not_2_out, not_3_out);
  and and_9 (and_9_out[0], third[0], not_1_out, Cin[1], not_3_out);
  and and_10 (and_9_out[1], third[1], not_1_out, Cin[1], not_3_out);
  and and_11 (and_9_out[2], third[2], not_1_out, Cin[1], not_3_out);
  and and_12 (and_9_out[3], third[3], not_1_out, Cin[1], not_3_out);
  and and_13 (and_13_out[0], fourth[0], Cin[0], Cin[1], not_3_out);
  and and_14 (and_13_out[1], fourth[1], Cin[0], Cin[1], not_3_out);
  and and_15 (and_13_out[2], fourth[2], Cin[0], Cin[1], not_3_out);
  and and_16 (and_13_out[3], fourth[3], Cin[0], Cin[1], not_3_out);
  and and_17 (and_17_out[0], fifth[0], not_1_out, not_2_out, Cin[2]);
  and and_18 (and_17_out[1], fifth[1], not_1_out, not_2_out, Cin[2]);
  and and_19 (and_17_out[2], fifth[2], not_1_out, not_2_out, Cin[2]);
  and and_20 (and_17_out[3], fifth[3], not_1_out, not_2_out, Cin[2]);
  assign out_7 = and_1_out | and_5_out | and_9_out | and_13_out | and_17_out;  // OR_Gate or_1, 4 bits wide
endmodule

module counterz (
  input  power,
  input  split,
  output [2:0] count
);

  wire and_1_out, and_2_out;

  T_Flip_Flop t_ff_1 (.T(power), .clk(split), .Q(count[0]), .reset(and_2_out));  // open: Qn, preset
  T_Flip_Flop t_ff_2 (.T(count[0]), .clk(split), .Q(count[1]), .reset(and_2_out));  // open: Qn, preset
  and and_1 (and_1_out, count[0], count[1]);
  T_Flip_Flop t_ff_3 (.T(and_1_out), .clk(split), .Q(count[2]), .reset(and_2_out));  // open: Qn, preset
  and and_2 (and_2_out, count[0], count[2]);
endmodule
