// Logisim project stage7__.circ as structural Verilog: 5 circuits, main circuit main
module main (
);

  wire and_1_out, and_2_out, and_3_out, and_4_out, and_5_out, and_6_out, and_7_out, and_8_out, and_9_out,
       and_10_out, and_11_out, and_12_out, and_13_out, and_14_out, button_1_out, button_2_out, button_3_out,
       clock_1_out, j_k_ff_1_q, j_k_ff_2_q, j_k_ff_3_q, j_k_ff_4_q, j_k_ff_5_q, j_k_ff_6_q, j_k_ff_7_q,
       j_k_ff_8_q, j_k_ff_9_q, j_k_ff_10_q, j_k_ff_11_q, j_k_ff_12_q, j_k_ff_13_q, j_k_ff_14_q, j_k_ff_15_q,
       or_1_out, or_2_out, or_3_out, or_4_out, t_ff_1_q;
  wire [2:0] d_ff_4_q, d_ff_16_q;
  wire [3:0] d_ff_1_q, d_ff_2_q, d_ff_3_q, split_record_1_out_18, split_record_1_out_19,
       split_record_1_out_20, split_record_1_out_21, split_record_2_out_18, split_record_2_out_19,
       split_record_2_out_20, split_record_2_out_21, split_record_3_out_18, split_record_3_out_19,
       split_record_3_out_20, split_record_3_out_21, split_record_4_out_18, split_record_4_out_19,
       split_record_4_out_20, split_record_4_out_21, split_time_1_out_7, split_time_2_out_7,
       split_time_3_out_7;

  Hex_Digit_Display hex_digit_display_1 (.value(d_ff_3_q));  // open: dp
  Hex_Digit_Display hex_digit_display_2 (.value(d_ff_2_q));  // open: dp
  Button button_1 (.out(button_1_out));
  Hex_Digit_Display hex_digit_display_3 (.value({1'b0, d_ff_4_q}));  // open: dp
  Hex_Digit_Display hex_digit_display_4 (.value(d_ff_1_q));  // open: dp
  Button button_2 (.out(button_2_out));
  Button button_3 (.out(button_3_out));
  Hex_Digit_Display hex_digit_display_5 (.value(split_time_3_out_7));  // open: dp
  Hex_Digit_Display hex_digit_display_6 (.value(split_time_2_out_7));  // open: dp
  LED led_1 (.in(t_ff_1_q));
  Hex_Digit_Display hex_digit_display_7 (.value({1'b0, d_ff_16_q}));  // open: dp
  T_Flip_Flop t_ff_1 (.T(1'b1), .clk(button_1_out), .Q(t_ff_1_q), .reset(button_3_out));  // open: Qn, preset
  Hex_Digit_Display hex_digit_display_8 (.value(split_time_1_out_7));  // open: dp
  Clock clock_1 (.out(clock_1_out));
  J_K_Flip_Flop j_k_ff_1 (
    .J(t_ff_1_q), .K(t_ff_1_q), .clk(clock_1_out), .Q(j_k_ff_1_q), .reset(or_1_out));  // open: Qn, preset
  J_K_Flip_Flop j_k_ff_2 (
    .J(t_ff_1_q), .K(t_ff_1_q), .clk(or_2_out), .Q(j_k_ff_2_q), .reset(or_3_out));  // open: Qn, preset
  J_K_Flip_Flop j_k_ff_3 (.J(1'b1), .K(1'b1), .clk(or_3_out), .Q(j_k_ff_3_q), .reset(or_4_out));  // open: Qn, preset
  and and_1 (and_1_out, t_ff_1_q, j_k_ff_1_q);
  D_Flip_Flop #(.trigger("falling")) d_ff_1 (
    .D(j_k_ff_1_q), .clk(clock_1_out), .Q(d_ff_1_q[0]), .reset(button_3_out));  // open: Qn, preset
  J_K_Flip_Flop j_k_ff_4 (.J(1'b1), .K(1'b1), .clk(or_1_out), .Q(j_k_ff_4_q), .reset(or_2_out));  // open: Qn, preset
  and and_2 (and_2_out, t_ff_1_q, j_k_ff_2_q);
  D_Flip_Flop #(.trigger("falling")) d_ff_2 (
    .D(j_k_ff_2_q), .clk(clock_1_out), .Q(d_ff_2_q[0]), .reset(button_3_out));  // open: Qn, preset
  D_Flip_Flop #(.trigger("falling")) d_ff_3 (
    .D(j_k_ff_3_q), .clk(clock_1_out), .Q(d_ff_3_q[0]), .reset(button_3_out));  // open: Qn, preset
  J_K_Flip_Flop j_k_ff_5 (
    .J(and_1_out), .K(and_1_out), .clk(clock_1_out), .Q(j_k_ff_5_q), .reset(or_1_out));  // open: Qn, preset
  D_Flip_Flop #(.trigger("falling")) d_ff_4 (
    .D(j_k_ff_4_q), .clk(clock_1_out), .Q(d_ff_4_q[0]), .reset(button_3_out));  // open: Qn, preset
  J_K_Flip_Flop j_k_ff_6 (
    .J(and_2_out), .K(and_2_out), .clk(or_2_out), .Q(j_k_ff_6_q), .reset(or_3_out));  // open: Qn, preset
  J_K_Flip_Flop j_k_ff_7 (
    .J(j_k_ff_3_q), .K(j_k_ff_3_q), .clk(or_3_out), .Q(j_k_ff_7_q), .reset(or_4_out));  // open: Qn, preset
  and and_3 (and_3_out, and_1_out, j_k_ff_5_q);
  D_Flip_Flop #(.trigger("falling")) d_ff_5 (
    .D(j_k_ff_5_q), .clk(clock_1_out), .Q(d_ff_1_q[1]), .reset(button_3_out));  // open: Qn, preset
  J_K_Flip_Flop j_k_ff_8 (
    .J(j_k_ff_4_q), .K(j_k_ff_4_q), .clk(or_1_out), .Q(j_k_ff_8_q), .reset(or_2_out));  // open: Qn, preset
  and and_4 (and_4_out, and_2_out, j_k_ff_6_q);
  D_Flip_Flop #(.trigger("falling")) d_ff_6 (
    .D(j_k_ff_6_q), .clk(clock_1_out), .Q(d_ff_2_q[1]), .reset(button_3_out));  // open: Qn, preset
  and and_5 (and_5_out, j_k_ff_3_q, j_k_ff_7_q);
  D_Flip_Flop #(.trigger("falling")) d_ff_7 (
    .D(j_k_ff_7_q), .clk(clock_1_out), .Q(d_ff_3_q[1]), .reset(button_3_out));  // open: Qn, preset
  J_K_Flip_Flop j_k_ff_9 (
    .J(and_3_out), .K(and_3_out), .clk(clock_1_out), .Q(j_k_ff_9_q), .reset(or_1_out));  // open: Qn, preset
  and and_6 (and_6_out, j_k_ff_4_q, j_k_ff_8_q);
  D_Flip_Flop #(.trigger("falling")) d_ff_8 (
    .D(j_k_ff_8_q), .clk(clock_1_out), .Q(d_ff_4_q[1]), .reset(button_3_out));  // open: Qn, preset
  J_K_Flip_Flop j_k_ff_10 (
    .J(and_4_out), .K(and_4_out), .clk(or_2_out), .Q(j_k_ff_10_q), .reset(or_3_out));  // open: Qn, preset
  J_K_Flip_Flop j_k_ff_11 (
    .J(and_5_out), .K(and_5_out), .clk(or_3_out), .Q(j_k_ff_11_q), .reset(or_4_out));  // open: Qn, preset
  and and_7 (and_7_out, and_3_out, j_k_ff_9_q);
  D_Flip_Flop #(.trigger("falling")) d_ff_9 (
    .D(j_k_ff_9_q), .clk(clock_1_out), .Q(d_ff_1_q[2]), .reset(button_3_out));  // open: Qn, preset
  J_K_Flip_Flop j_k_ff_12 (
    .J(and_6_out), .K(and_6_out), .clk(or_1_out), .Q(j_k_ff_12_q), .reset(or_2_out));  // open: Qn, preset
  and and_8 (and_8_out, and_4_out, j_k_ff_10_q);
  D_Flip_Flop #(.trigger("falling")) d_ff_10 (
    .D(j_k_ff_10_q), .clk(clock_1_out), .Q(d_ff_2_q[2]), .reset(button_3_out));  // open: Qn, preset
  and and_9 (and_9_out, and_5_out, j_k_ff_11_q);
  D_Flip_Flop #(.trigger("falling")) d_ff_11 (
    .D(j_k_ff_11_q), .clk(clock_1_out), .Q(d_ff_3_q[2]), .reset(button_3_out));  // open: Qn, preset
  J_K_Flip_Flop j_k_ff_13 (
    .J(and_7_out), .K(and_7_out), .clk(clock_1_out), .Q(j_k_ff_13_q), .reset(or_1_out));  // open: Qn, preset
  and and_10 (and_10_out, j_k_ff_8_q, j_k_ff_12_q);
  D_Flip_Flop #(.trigger("falling")) d_ff_12 (
    .D(j_k_ff_12_q), .clk(clock_1_out), .Q(d_ff_4_q[2]), .reset(button_3_out));  // open: Qn, preset
  J_K_Flip_Flop j_k_ff_14 (
    .J(and_8_out), .K(and_8_out), .clk(or_2_out), .Q(j_k_ff_14_q), .reset(or_3_out));  // open: Qn, preset
  J_K_Flip_Flop j_k_ff_15 (
    .J(and_9_out), .K(and_9_out), .clk(or_3_out), .Q(j_k_ff_15_q), .reset(or_4_out));  // open: Qn, preset
  and and_11 (and_11_out, j_k_ff_5_q, j_k_ff_13_q);
  D_Flip_Flop #(.trigger("falling")) d_ff_13 (
    .D(j_k_ff_13_q), .clk(clock_1_out), .Q(d_ff_1_q[3]), .reset(button_3_out));  // open: Qn, preset
  and and_12 (and_12_out, j_k_ff_6_q, j_k_ff_14_q);
  D_Flip_Flop #(.trigger("falling")) d_ff_14 (
    .D(j_k_ff_14_q), .clk(clock_1_out), .Q(d_ff_2_q[3]), .reset(button_3_out));  // open: Qn, preset
  and and_13 (and_13_out, j_k_ff_7_q, j_k_ff_15_q);
  D_Flip_Flop #(.trigger("falling")) d_ff_15 (
    .D(j_k_ff_15_q), .clk(clock_1_out), .Q(d_ff_3_q[3]), .reset(button_3_out));  // open: Qn, preset
  or or_1 (or_1_out, and_11_out, button_3_out);
  or or_2 (or_2_out, and_10_out, button_3_out);
  or or_3 (or_3_out, and_12_out, button_3_out);
  or or_4 (or_4_out, and_13_out, button_3_out);
  and and_14 (and_14_out, t_ff_1_q, button_2_out);
  D_Flip_Flop d_ff_16 (.D(d_ff_4_q[0]), .clk(and_14_out), .Q(d_ff_16_q[0]), .reset(button_3_out));  // open: Qn, preset
  D_Flip_Flop d_ff_17 (.D(d_ff_4_q[1]), .clk(and_14_out), .Q(d_ff_16_q[1]), .reset(button_3_out));  // open: Qn, preset
  D_Flip_Flop d_ff_18 (.D(d_ff_4_q[2]), .clk(and_14_out), .Q(d_ff_16_q[2]), .reset(button_3_out));  // open: Qn, preset
  split_time split_time_1 (
    .in_3(d_ff_1_q[0]), .in_4(d_ff_1_q[1]), .in_5(d_ff_1_q[2]), .in_6(d_ff_1_q[3]), .split(and_14_out),
    .reset(button_3_out), .out_7(split_time_1_out_7));
  split_time split_time_2 (
    .in_3(d_ff_2_q[0]), .in_4(d_ff_2_q[1]), .in_5(d_ff_2_q[2]), .in_6(d_ff_2_q[3]), .split(and_14_out),
    .reset(button_3_out), .out_7(split_time_2_out_7));
  split_time split_time_3 (
    .in_3(d_ff_3_q[0]), .in_4(d_ff_3_q[1]), .in_5(d_ff_3_q[2]), .in_6(d_ff_3_q[3]), .split(and_14_out),
    .reset(button_3_out), .out_7(split_time_3_out_7));
  split_record split_record_1 (
    .split(and_14_out), .reset(button_3_out), .second1(split_time_1_out_7[0]),
    .second2(split_time_1_out_7[1]), .second3(split_time_1_out_7[2]), .second4(split_time_1_out_7[3]),
    .tens1(d_ff_16_q[0]), .tens2(d_ff_16_q[1]), .tens3(d_ff_16_q[2]), .minute1(split_time_2_out_7[0]),
    .minute2(split_time_2_out_7[1]), .minute3(split_time_2_out_7[2]), .minute4(split_time_2_out_7[3]),
    .minutes1(split_time_3_out_7[0]), .minutes2(split_time_3_out_7[1]), .minutes3(split_time_3_out_7[2]),
    .minutes4(split_time_3_out_7[3]), .out_18(split_record_1_out_18), .out_19(split_record_1_out_19),
    .out_20(split_record_1_out_20), .out_21(split_record_1_out_21));
  Hex_Digit_Display hex_digit_display_9 (.value(split_record_1_out_18));  // open: dp
  Hex_Digit_Display hex_digit_display_10 (.value(split_record_1_out_19));  // open: dp
  Hex_Digit_Display hex_digit_display_11 (.value(split_record_1_out_20));  // open: dp
  Hex_Digit_Display hex_digit_display_12 (.value(split_record_1_out_21));  // open: dp
  Hex_Digit_Display hex_digit_display_13 (.value(split_record_2_out_18));  // open: dp
  split_record split_record_2 (
    .split(and_14_out), .reset(button_3_out), .second1(split_record_1_out_21[0]),
    .second2(split_record_1_out_21[1]), .second3(split_record_1_out_21[2]),
    .second4(split_record_1_out_21[3]), .tens1(split_record_1_out_20[0]), .tens2(split_record_1_out_20[1]),
    .tens3(split_record_1_out_20[2]), .minute1(split_record_1_out_19[0]), .minute2(split_record_1_out_19[1]),
    .minute3(split_record_1_out_19[2]), .minute4(split_record_1_out_19[3]),
    .minutes1(split_record_1_out_18[0]), .minutes2(split_record_1_out_18[1]),
    .minutes3(split_record_1_out_18[2]), .minutes4(split_record_1_out_18[3]), .out_18(split_record_2_out_18),
    .out_19(split_record_2_out_19), .out_20(split_record_2_out_20), .out_21(split_record_2_out_21));
  Hex_Digit_Display hex_digit_display_14 (.value(split_record_2_out_19));  // open: dp
  Hex_Digit_Display hex_digit_display_15 (.value(split_record_2_out_20));  // open: dp
  Hex_Digit_Display hex_digit_display_16 (.value(split_record_2_out_21));  // open: dp
  Hex_Digit_Display hex_digit_display_17 (.value(split_record_3_out_18));  // open: dp
  split_record split_record_3 (
    .split(and_14_out), .reset(button_3_out), .second1(split_record_2_out_21[0]),
    .second2(split_record_2_out_21[1]), .second3(split_record_2_out_21[2]),
    .second4(split_record_2_out_21[3]), .tens1(split_record_2_out_20[0]), .tens2(split_record_2_out_20[1]),
    .tens3(split_record_2_out_20[2]), .minute1(split_record_2_out_19[0]), .minute2(split_record_2_out_19[1]),
    .minute3(split_record_2_out_19[2]), .minute4(split_record_2_out_19[3]),
    .minutes1(split_record_2_out_18[0]), .minutes2(split_record_2_out_18[1]),
    .minutes3(split_record_2_out_18[2]), .minutes4(split_record_2_out_18[3]), .out_18(split_record_3_out_18),
    .out_19(split_record_3_out_19), .out_20(split_record_3_out_20), .out_21(split_record_3_out_21));
  Hex_Digit_Display hex_digit_display_18 (.value(split_record_3_out_19));  // open: dp
  Hex_Digit_Display hex_digit_display_19 (.value(split_record_3_out_20));  // open: dp
  Hex_Digit_Display hex_digit_display_20 (.value(split_record_3_out_21));  // open: dp
  split_record split_record_4 (
    .split(and_14_out), .reset(button_3_out), .second1(split_record_3_out_21[0]),
    .second2(split_record_3_out_21[1]), .second3(split_record_3_out_21[2]),
    .second4(split_record_3_out_21[3]), .tens1(split_record_3_out_20[0]), .tens2(split_record_3_out_20[1]),
    .tens3(split_record_3_out_20[2]), .minute1(split_record_3_out_19[0]), .minute2(split_record_3_out_19[1]),
    .minute3(split_record_3_out_19[2]), .minute4(split_record_3_out_19[3]),
    .minutes1(split_record_3_out_18[0]), .minutes2(split_record_3_out_18[1]),
    .minutes3(split_record_3_out_18[2]), .minutes4(split_record_3_out_18[3]), .out_18(split_record_4_out_18),
    .out_19(split_record_4_out_19), .out_20(split_record_4_out_20), .out_21(split_record_4_out_21));
  Hex_Digit_Display hex_digit_display_21 (.value(split_record_4_out_18));  // open: dp
  Hex_Digit_Display hex_digit_display_22 (.value(split_record_4_out_19));  // open: dp
  Hex_Digit_Display hex_digit_display_23 (.value(split_record_4_out_20));  // open: dp
  Hex_Digit_Display hex_digit_display_24 (.value(split_record_4_out_21));  // open: dp
  // also tied to GND on the sheet: {split_record_1_out_20[3], split_record_2_out_20[3], split_record_3_out_20[3]}

  // Notes on the sheet:
  //   Elapsed Time
  //   Minutes
  //   :
  //   Start / Stop
  //   Seconds
  //   Stopwatch Interface
  //   Split
  //   Reset
  //   Minutes
  //   Clock Started
  //   Split Time
  //   :
  //   Seconds
  //   Minutes
  //   Split 2
  //   Seconds
  //   :
  //   Minutes
  //   Split 3
  //   :
  //   Seconds
  //   Split 4
  //   Minutes
  //   :
  //   Seconds
  //   Minutes
  //   Split 5
  //   :
  //   Seconds
endmodule

module split_time (
  input  split,
  input  reset,
  input  in_3,
  input  in_4,
  input  in_5,
  input  in_6,
  output [3:0] out_7
);

  D_Flip_Flop d_ff_1 (.D(in_3), .clk(split), .Q(out_7[0]), .reset(reset));  // open: Qn, preset
  D_Flip_Flop d_ff_2 (.D(in_4), .clk(split), .Q(out_7[1]), .reset(reset));  // open: Qn, preset
  D_Flip_Flop d_ff_3 (.D(in_5), .clk(split), .Q(out_7[2]), .reset(reset));  // open: Qn, preset
  D_Flip_Flop d_ff_4 (.D(in_6), .clk(split), .Q(out_7[3]), .reset(reset));  // open: Qn, preset
endmodule

module split_record (
  input  split,
  input  reset,
  input  second1,
  input  second2,
  input  second3,
  input  second4,
  input  tens1,
  input  tens2,
  input  tens3,
  input  minute1,
  input  minute2,
  input  minute3,
  input  minute4,
  input  minutes1,
  input  minutes2,
  input  minutes3,
  input  minutes4,
  output [3:0] out_18,
  output [3:0] out_19,
  output [3:0] out_20,
  output [3:0] out_21
);

  D_Flip_Flop d_ff_1 (.D(second1), .clk(split), .Q(out_21[0]), .reset(reset));  // open: Qn, preset
  D_Flip_Flop d_ff_2 (.D(minute1), .clk(split), .Q(out_19[0]), .reset(reset));  // open: Qn, preset
  D_Flip_Flop d_ff_3 (.D(minutes1), .clk(split), .Q(out_18[0]), .reset(reset));  // open: Qn, preset
  D_Flip_Flop d_ff_4 (.D(tens1), .clk(split), .Q(out_20[0]), .reset(reset));  // open: Qn, preset
  D_Flip_Flop d_ff_5 (.D(second2), .clk(split), .Q(out_21[1]), .reset(reset));  // open: Qn, preset
  D_Flip_Flop d_ff_6 (.D(tens2), .clk(split), .Q(out_20[1]), .reset(reset));  // open: Qn, preset
  D_Flip_Flop d_ff_7 (.D(minute2), .clk(split), .Q(out_19[1]), .reset(reset));  // open: Qn, preset
  D_Flip_Flop d_ff_8 (.D(minutes2), .clk(split), .Q(out_18[1]), .reset(reset));  // open: Qn, preset
  D_Flip_Flop d_ff_9 (.D(second3), .clk(split), .Q(out_21[2]), .reset(reset));  // open: Qn, preset
  D_Flip_Flop d_ff_10 (.D(tens3), .clk(split), .Q(out_20[2]), .reset(reset));  // open: Qn, preset
  D_Flip_Flop d_ff_11 (.D(minute3), .clk(split), .Q(out_19[2]), .reset(reset));  // open: Qn, preset
  D_Flip_Flop d_ff_12 (.D(minutes3), .clk(split), .Q(out_18[2]), .reset(reset));  // open: Qn, preset
  D_Flip_Flop d_ff_13 (.D(second4), .clk(split), .Q(out_21[3]), .reset(reset));  // open: Qn, preset
  D_Flip_Flop d_ff_14 (.D(minute4), .clk(split), .Q(out_19[3]), .reset(reset));  // open: Qn, preset
  D_Flip_Flop d_ff_15 (.D(minutes4), .clk(split), .Q(out_18[3]), .reset(reset));  // open: Qn, preset

  assign out_20[3] = 1'b0;
endmodule

module plex (
  input  in_1,
  input  in_2,
  input  in_3,
  input  in_4,
  input  in_5,
  input  in_6,
  input  in_7,
  input  in_8,
  input  in_9,
  input  in_10,
  input  in_11,
  input  in_12,
  input  in_13,
  input  in_14,
  input  in_15,
  input  in_16,
  input  in_17,
  input  in_18,
  input  in_19,
  input  in_20,
  input  [3:0] seconds,
  input  [3:0] sectens,
  input  [3:0] minute,
  input  [3:0] minutetens,
  output [3:0] savedSecOnes,
  output [3:0] savedSecTens,
  output [3:0] savedMinOnes,
  output [3:0] savedMinTens
);

  wire [3:0] and_3_out, and_4_out, and_5_out, and_6_out, and_9_out, and_10_out, and_11_out, and_13_out,
       and_15_out, and_16_out, and_17_out, and_18_out, and_21_out, and_22_out, and_23_out, and_24_out,
       and_27_out, and_28_out, and_29_out, and_30_out, save_split_1_outminones, save_split_1_outmintens,
       save_split_1_outsecone, save_split_1_outsectens, save_split_2_outminones, save_split_2_outmintens,
       save_split_2_outsecone, save_split_2_outsectens, save_split_3_outminones, save_split_3_outmintens,
       save_split_3_outsecone, save_split_3_outsectens, save_split_4_outminones, save_split_4_outmintens,
       save_split_4_outsecone, save_split_4_outsectens, save_split_5_outminones, save_split_5_outmintens,
       save_split_5_outsecone, save_split_5_outsectens;
  wire [3:3] and_1_out, and_7_out, and_12_out, and_19_out, and_25_out;

  and and_1 (and_1_out[3], in_6, in_7, in_8);
  // AND_Gate and_2 has open pins: in0=and_1_out[3], in1=in_1, out=open
  assign savedSecOnes = and_6_out | and_13_out | and_18_out | and_24_out | and_30_out;  // OR_Gate or_1, 4 bits wide
  assign savedSecTens = and_5_out | and_11_out | and_17_out | and_23_out | and_29_out;  // OR_Gate or_2, 4 bits wide
  assign savedMinOnes = and_4_out | and_10_out | and_16_out | and_22_out | and_28_out;  // OR_Gate or_3, 4 bits wide
  assign savedMinTens = and_3_out | and_9_out | and_15_out | and_21_out | and_27_out;  // OR_Gate or_4, 4 bits wide
  Hex_Digit_Display hex_digit_display_1 (.value(save_split_1_outmintens));  // open: dp
  Hex_Digit_Display hex_digit_display_2 (.value(save_split_1_outminones));  // open: dp
  assign and_3_out = {4{and_1_out[3]}} & save_split_1_outmintens;  // AND_Gate and_3, 4 bits wide
  Hex_Digit_Display hex_digit_display_3 (.value(save_split_1_outsectens));  // open: dp
  assign and_4_out = save_split_1_outminones;  // AND_Gate and_4, 4 bits wide AND_Gate
  assign and_5_out = save_split_1_outsectens;  // AND_Gate and_5, 4 bits wide AND_Gate
  save_split save_split_1 (
    .secondOne(seconds), .secondTens(sectens), .minuteOnes(minute), .minuteTens(minutetens),
    .OutMinTens(save_split_1_outmintens), .OutMinOnes(save_split_1_outminones),
    .OutSecTens(save_split_1_outsectens), .OutSecOne(save_split_1_outsecone));  // open: split, reset
  Hex_Digit_Display hex_digit_display_4 (.value(save_split_1_outsecone));  // open: dp
  assign and_6_out = save_split_1_outsecone;  // AND_Gate and_6, 4 bits wide AND_Gate
  and and_7 (and_7_out[3], in_9, in_10, in_11);
  // AND_Gate and_8 has open pins: in0=and_7_out[3], in1=in_2, out=open
  Hex_Digit_Display hex_digit_display_5 (.value(save_split_2_outmintens));  // open: dp
  Hex_Digit_Display hex_digit_display_6 (.value(save_split_2_outminones));  // open: dp
  assign and_9_out = {4{and_7_out[3]}} & save_split_2_outmintens;  // AND_Gate and_9, 4 bits wide
  assign and_10_out = save_split_2_outminones;  // AND_Gate and_10, 4 bits wide AND_Gate
  Hex_Digit_Display hex_digit_display_7 (.value(save_split_2_outsectens));  // open: dp
  assign and_11_out = save_split_2_outsectens;  // AND_Gate and_11, 4 bits wide AND_Gate
  and and_12 (and_12_out[3], in_12, in_13, in_14);
  save_split save_split_2 (
    .secondOne(seconds), .secondTens(sectens), .minuteOnes(minute), .minuteTens(minutetens),
    .OutMinTens(save_split_2_outmintens), .OutMinOnes(save_split_2_outminones),
    .OutSecTens(save_split_2_outsectens), .OutSecOne(save_split_2_outsecone));  // open: split, reset
  Hex_Digit_Display hex_digit_display_8 (.value(save_split_2_outsecone));  // open: dp
  assign and_13_out = save_split_2_outsecone;  // AND_Gate and_13, 4 bits wide AND_Gate
  // AND_Gate and_14 has open pins: in0=and_12_out[3], in1=in_3, out=open
  Hex_Digit_Display hex_digit_display_9 (.value(save_split_3_outmintens));  // open: dp
  assign and_15_out = {4{and_12_out[3]}} & save_split_3_outmintens;  // AND_Gate and_15, 4 bits wide
  Hex_Digit_Display hex_digit_display_10 (.value(save_split_3_outminones));  // open: dp
  Hex_Digit_Display hex_digit_display_11 (.value(save_split_3_outsectens));  // open: dp
  assign and_16_out = save_split_3_outminones;  // AND_Gate and_16, 4 bits wide AND_Gate
  Hex_Digit_Display hex_digit_display_12 (.value(save_split_3_outsecone));  // open: dp
  assign and_17_out = save_split_3_outsectens;  // AND_Gate and_17, 4 bits wide AND_Gate
  assign and_18_out = save_split_3_outsecone;  // AND_Gate and_18, 4 bits wide AND_Gate
  and and_19 (and_19_out[3], in_15, in_16, in_17);
  // AND_Gate and_20 has open pins: in0=and_19_out[3], in1=in_4, out=open
  save_split save_split_3 (
    .secondOne(seconds), .secondTens(sectens), .minuteOnes(minute), .minuteTens(minutetens),
    .OutMinTens(save_split_3_outmintens), .OutMinOnes(save_split_3_outminones),
    .OutSecTens(save_split_3_outsectens), .OutSecOne(save_split_3_outsecone));  // open: split, reset
  Hex_Digit_Display hex_digit_display_13 (.value(save_split_4_outmintens));  // open: dp
  Hex_Digit_Display hex_digit_display_14 (.value(save_split_4_outminones));  // open: dp
  assign and_21_out = {4{and_19_out[3]}} & save_split_4_outmintens;  // AND_Gate and_21, 4 bits wide
  Hex_Digit_Display hex_digit_display_15 (.value(save_split_4_outsectens));  // open: dp
  assign and_22_out = save_split_4_outminones;  // AND_Gate and_22, 4 bits wide AND_Gate
  assign and_23_out = save_split_4_outsectens;  // AND_Gate and_23, 4 bits wide AND_Gate
  save_split save_split_4 (
    .secondOne(seconds), .secondTens(sectens), .minuteOnes(minute), .minuteTens(minutetens),
    .OutMinTens(save_split_4_outmintens), .OutMinOnes(save_split_4_outminones),
    .OutSecTens(save_split_4_outsectens), .OutSecOne(save_split_4_outsecone));  // open: split, reset
  Hex_Digit_Display hex_digit_display_16 (.value(save_split_4_outsecone));  // open: dp
  assign and_24_out = save_split_4_outsecone;  // AND_Gate and_24, 4 bits wide AND_Gate
  and and_25 (and_25_out[3], in_18, in_19, in_20);
  // AND_Gate and_26 has open pins: in0=and_25_out[3], in1=in_5, out=open
  Hex_Digit_Display hex_digit_display_17 (.value(save_split_5_outmintens));  // open: dp
  Hex_Digit_Display hex_digit_display_18 (.value(save_split_5_outminones));  // open: dp
  assign and_27_out = {4{and_25_out[3]}} & save_split_5_outmintens;  // AND_Gate and_27, 4 bits wide
  assign and_28_out = save_split_5_outminones;  // AND_Gate and_28, 4 bits wide AND_Gate
  Hex_Digit_Display hex_digit_display_19 (.value(save_split_5_outsectens));  // open: dp
  Hex_Digit_Display hex_digit_display_20 (.value(save_split_5_outsecone));  // open: dp
  assign and_29_out = save_split_5_outsectens;  // AND_Gate and_29, 4 bits wide AND_Gate
  assign and_30_out = save_split_5_outsecone;  // AND_Gate and_30, 4 bits wide AND_Gate
  save_split save_split_5 (
    .secondOne(seconds), .secondTens(sectens), .minuteOnes(minute), .minuteTens(minutetens),
    .OutMinTens(save_split_5_outmintens), .OutMinOnes(save_split_5_outminones),
    .OutSecTens(save_split_5_outsectens), .OutSecOne(save_split_5_outsecone));  // open: split, reset

  // Notes on the sheet:
  //   Minutes
  //   Seconds
  //   :
  //   Minutes
  //   Seconds
  //   :
  //   Minutes
  //   :
  //   Seconds
  //   Minutes
  //   Seconds
  //   :
  //   Minutes
  //   :
  //   Seconds
endmodule

module save_split (
  input  split,
  input  reset,
  input  [3:0] secondOne,
  input  [3:0] secondTens,
  input  [3:0] minuteOnes,
  input  [3:0] minuteTens,
  output [3:0] OutMinTens,
  output [3:0] OutMinOnes,
  output [3:0] OutSecTens,
  output [3:0] OutSecOne
);

  D_Flip_Flop d_ff_1 (.D(secondOne[0]), .clk(split), .Q(OutSecOne[0]), .reset(reset));  // open: Qn, preset
  D_Flip_Flop d_ff_2 (.D(minuteOnes[0]), .clk(split), .Q(OutMinOnes[0]), .reset(reset));  // open: Qn, preset
  D_Flip_Flop d_ff_3 (.D(minuteTens[0]), .clk(split), .Q(OutMinTens[0]), .reset(reset));  // open: Qn, preset
  D_Flip_Flop d_ff_4 (.D(secondOne[1]), .clk(split), .Q(OutSecOne[1]), .reset(reset));  // open: Qn, preset
  D_Flip_Flop d_ff_5 (.D(secondTens[0]), .clk(split), .Q(OutSecTens[0]), .reset(reset));  // open: Qn, preset
  D_Flip_Flop d_ff_6 (.D(minuteOnes[1]), .clk(split), .Q(OutMinOnes[1]), .reset(reset));  // open: Qn, preset
  D_Flip_Flop d_ff_7 (.D(minuteTens[1]), .clk(split), .Q(OutMinTens[1]), .reset(reset));  // open: Qn, preset
  D_Flip_Flop d_ff_8 (.D(secondTens[1]), .clk(split), .Q(OutSecTens[1]), .reset(reset));  // open: Qn, preset
  D_Flip_Flop d_ff_9 (.D(secondOne[2]), .clk(split), .Q(OutSecOne[2]), .reset(reset));  // open: Qn, preset
  D_Flip_Flop d_ff_10 (.D(minuteOnes[2]), .clk(split), .Q(OutMinOnes[2]), .reset(reset));  // open: Qn, preset
  D_Flip_Flop d_ff_11 (.D(minuteTens[2]), .clk(split), .Q(OutMinTens[2]), .reset(reset));  // open: Qn, preset
  D_Flip_Flop d_ff_12 (.D(secondOne[3]), .clk(split), .Q(OutSecOne[3]), .reset(reset));  // open: Qn, preset
  D_Flip_Flop d_ff_13 (.D(secondTens[2]), .clk(split), .Q(OutSecTens[2]), .reset(reset));  // open: Qn, preset
  D_Flip_Flop d_ff_14 (.D(minuteOnes[3]), .clk(split), .Q(OutMinOnes[3]), .reset(reset));  // open: Qn, preset
  D_Flip_Flop d_ff_15 (.D(minuteTens[3]), .clk(split), .Q(OutMinTens[3]), .reset(reset));  // open: Qn, preset

  assign OutSecTens[3] = 1'b0;
  // also tied to GND on the sheet: secondTens[3]
endmodule
