// Logisim project Lab01.circ as structural Verilog: 1 circuit, main circuit main
module main (
  input  AND_GATE,
  input  in_2,
  input  in_3,
  input  in_4,
  input  in_5,
  input  in_6,
  input  in_7,
  input  in_8,
  input  NOT_GATE,
  input  in_10,
  input  in_11,
  input  XOR_GATE,
  input  in_13,
  input  in_14,
  input  in_15,
  input  in_16,
  input  in_17,
  input  in_18,
  input  in_19,
  input  in_20,
  input  in_21,
  input  in_22,
  input  in_23,
  input  in_24,
  input  in_25,
  input  in_26,
  input  in_27,
  input  in_28,
  input  in_29,
  input  in_30,
  input  in_31,
  input  in_32,
  input  in_33,
  input  in_34
);

  wire and_1_out, and_2_out, and_3_out, and_4_out, and_5_out, and_6_out, and_7_out, and_8_out, and_9_out,
       and_10_out, and_11_out, and_12_out, not_1_out, not_2_out, not_3_out, not_4_out, not_5_out, not_6_out,
       not_7_out, not_8_out, not_9_out, not_10_out, not_11_out, not_12_out, not_13_out, not_14_out,
       not_15_out, not_16_out, or_1_out, or_2_out, or_3_out, or_4_out, xor_1_out, xor_2_out, xor_3_out,
       xor_4_out, xor_5_out, xor_6_out;

  and and_1 (and_1_out, AND_GATE, in_3);
  and and_2 (and_2_out, in_5, in_7);
  not not_1 (not_1_out, NOT_GATE);
  not not_2 (not_2_out, in_10);
  xor xor_1 (xor_1_out, XOR_GATE, in_14);
  xor xor_2 (xor_2_out, in_15, in_17);
  xor xor_3 (xor_3_out, in_19, in_21);
  not not_3 (not_3_out, in_28);
  not not_4 (not_4_out, in_26);
  not not_5 (not_5_out, in_24);
  not not_6 (not_6_out, in_34);
  not not_7 (not_7_out, in_32);
  not not_8 (not_8_out, in_30);
  LED led_1 (.in(and_1_out));
  LED led_2 (.in(and_2_out));
  LED led_3 (.in(not_1_out));
  LED led_4 (.in(not_2_out));
  LED led_5 (.in(xor_1_out));
  LED led_6 (.in(xor_2_out));
  not not_9 (not_9_out, xor_3_out);
  LED led_7 (.in(not_9_out));
  and and_3 (and_3_out, in_24, in_26, in_28);
  and and_4 (and_4_out, in_30, in_32, in_34);
  and and_5 (and_5_out, not_3_out, not_4_out, not_5_out);
  and and_6 (and_6_out, not_6_out, not_7_out, not_8_out);
  xor xor_4 (xor_4_out, in_11, in_13);
  xor xor_5 (xor_5_out, in_16, in_18);
  xor xor_6 (xor_6_out, in_20, in_22);
  and and_7 (and_7_out, in_2, in_4);
  and and_8 (and_8_out, in_6, in_8);
  LED led_8 (.in(xor_4_out));
  LED led_9 (.in(xor_5_out));
  not not_10 (not_10_out, xor_6_out);
  or or_1 (or_1_out, and_5_out, and_3_out);
  LED led_10 (.in(or_1_out));
  or or_2 (or_2_out, and_6_out, and_4_out);
  LED led_11 (.in(or_2_out));
  LED led_12 (.in(and_7_out));
  LED led_13 (.in(and_8_out));
  LED led_14 (.in(not_10_out));
  not not_11 (not_11_out, in_27);
  not not_12 (not_12_out, in_25);
  not not_13 (not_13_out, in_23);
  and and_9 (and_9_out, in_23, in_25, in_27);
  not not_14 (not_14_out, in_33);
  not not_15 (not_15_out, in_31);
  not not_16 (not_16_out, in_29);
  and and_10 (and_10_out, in_29, in_31, in_33);
  and and_11 (and_11_out, not_11_out, not_12_out, not_13_out);
  and and_12 (and_12_out, not_14_out, not_15_out, not_16_out);
  or or_3 (or_3_out, and_11_out, and_9_out);
  LED led_15 (.in(or_3_out));
  or or_4 (or_4_out, and_12_out, and_10_out);
  LED led_16 (.in(or_4_out));
endmodule
