// Logisim project Lab02.circ as structural Verilog: 1 circuit, main circuit main
module main (
  input  input_1,
  input  input_2,
  input  Carry_In,
  input  Inp1,
  input  Inp2,
  input  Input_A,
  input  Input_B,
  input  Input_A_2,
  input  Input_B_2,
  input  Input_A_3,
  input  Input_B_3,
  input  Input_A_4,
  input  Input_B_4
);

  wire and_1_out, and_2_out, and_3_out, and_4_out, and_5_out, and_6_out, and_7_out, and_8_out, and_9_out,
       and_10_out, or_1_out, or_2_out, or_3_out, or_4_out, xor_1_out, xor_2_out, xor_3_out, xor_4_out,
       xor_5_out, xor_6_out, xor_7_out, xor_8_out, xor_9_out, xor_10_out;

  xor xor_1 (xor_1_out, input_1, input_2);
  and and_1 (and_1_out, input_2, input_1);
  LED led_1 (.in(xor_1_out));
  LED led_2 (.in(and_1_out));
  xor xor_2 (xor_2_out, Inp1, Inp2);
  and and_2 (and_2_out, Inp1, Inp2);
  xor xor_3 (xor_3_out, Input_A_2, Input_B_2);
  and and_3 (and_3_out, Input_A_2, Input_B_2);
  xor xor_4 (xor_4_out, Input_A_3, Input_B_3);
  and and_4 (and_4_out, Input_A_3, Input_B_3);
  xor xor_5 (xor_5_out, Input_A_4, Input_B_4);
  and and_5 (and_5_out, Input_A_4, Input_B_4);
  xor xor_6 (xor_6_out, Carry_In, xor_2_out);
  and and_6 (and_6_out, Carry_In, xor_2_out);
  xor xor_7 (xor_7_out, Input_A, Input_B);
  and and_7 (and_7_out, Input_B, Input_A);
  LED led_3 (.in(xor_6_out));
  LED led_4 (.in(xor_7_out));
  or or_1 (or_1_out, and_6_out, and_2_out);
  xor xor_8 (xor_8_out, and_7_out, xor_3_out);
  LED led_5 (.in(xor_8_out));
  and and_8 (and_8_out, and_7_out, xor_3_out);
  xor xor_9 (xor_9_out, or_2_out, xor_4_out);
  LED led_6 (.in(xor_9_out));
  and and_9 (and_9_out, or_2_out, xor_4_out);
  xor xor_10 (xor_10_out, or_3_out, xor_5_out);
  LED led_7 (.in(xor_10_out));
  and and_10 (and_10_out, or_3_out, xor_5_out);
  LED led_8 (.in(or_1_out));
  or or_2 (or_2_out, and_8_out, and_3_out);
  or or_3 (or_3_out, and_9_out, and_4_out);
  or or_4 (or_4_out, and_10_out, and_5_out);
  LED led_9 (.in(and_7_out));
  LED led_10 (.in(or_2_out));
  LED led_11 (.in(or_3_out));
  LED led_12 (.in(or_4_out));

  // Notes on the sheet:
  //   HALF ADDER
  //   sum
  //   FULL ADDER
  //   C out
  //   SUM
  //   Sum
  //   Sum
  //   Sum
  //   Sum
  //   C. Out
  //   4 BIT ADDER
  //   Carry
  //   Carry
  //   Carry
  //   Carry
endmodule
