// Logisim project Lab04.circ as structural Verilog: 1 circuit, main circuit main
module main (
  input  in_1,
  input  in_2,
  input  in_3,
  input  in_4
);

  wire and_1_out, and_2_out, clock_1_out, clock_2_out, clock_3_out, j_k_ff_1_q, j_k_ff_3_q, j_k_ff_5_q,
       j_k_ff_7_q, j_k_ff_8_q, j_k_ff_9_q;
  wire [2:0] j_k_ff_2_q;

  Clock clock_1 (.out(clock_1_out));
  Clock clock_2 (.out(clock_2_out));
  J_K_Flip_Flop #(.trigger("falling")) j_k_ff_1 (
    .J(in_1), .K(in_1), .clk(clock_1_out), .Q(j_k_ff_1_q));  // open: Qn, preset, reset
  J_K_Flip_Flop #(.trigger("falling")) j_k_ff_2 (
    .J(in_3), .K(in_3), .clk(clock_2_out), .Q(j_k_ff_2_q[0]), .reset(and_1_out));  // open: Qn, preset
  J_K_Flip_Flop #(.trigger("falling")) j_k_ff_3 (
    .J(in_1), .K(in_1), .clk(j_k_ff_1_q), .Q(j_k_ff_3_q));  // open: Qn, preset, reset
  LED led_1 (.in(j_k_ff_1_q));
  J_K_Flip_Flop #(.trigger("falling")) j_k_ff_4 (
    .J(in_3), .K(in_3), .clk(j_k_ff_2_q[0]), .Q(j_k_ff_2_q[1]), .reset(and_1_out));  // open: Qn, preset
  LED led_2 (.in(j_k_ff_2_q[0]));
  LED led_3 (.in(j_k_ff_3_q));
  LED led_4 (.in(j_k_ff_2_q[1]));
  J_K_Flip_Flop #(.trigger("falling")) j_k_ff_5 (
    .J(in_1), .K(in_1), .clk(j_k_ff_3_q), .Q(j_k_ff_5_q));  // open: Qn, preset, reset
  J_K_Flip_Flop #(.trigger("falling")) j_k_ff_6 (
    .J(in_3), .K(in_3), .clk(j_k_ff_2_q[1]), .Q(j_k_ff_2_q[2]), .reset(and_1_out));  // open: Qn, preset
  LED led_5 (.in(j_k_ff_5_q));
  LED led_6 (.in(j_k_ff_2_q[2]));
  and and_1 (and_1_out, j_k_ff_2_q[1], j_k_ff_2_q[2]);
  Hex_Digit_Display hex_digit_display_1 (.value({in_4, j_k_ff_2_q}));  // open: dp
  J_K_Flip_Flop #(.trigger("falling")) j_k_ff_7 (
    .J(in_2), .K(in_2), .clk(clock_3_out), .Q(j_k_ff_7_q));  // open: Qn, preset, reset
  Clock clock_3 (.out(clock_3_out));
  LED led_7 (.in(j_k_ff_7_q));
  J_K_Flip_Flop #(.trigger("falling")) j_k_ff_8 (
    .J(j_k_ff_7_q), .K(j_k_ff_7_q), .clk(clock_3_out), .Q(j_k_ff_8_q));  // open: Qn, preset, reset
  and and_2 (and_2_out, j_k_ff_7_q, j_k_ff_8_q);
  J_K_Flip_Flop #(.trigger("falling")) j_k_ff_9 (
    .J(and_2_out), .K(and_2_out), .clk(clock_3_out), .Q(j_k_ff_9_q));  // open: Qn, preset, reset
  LED led_8 (.in(j_k_ff_8_q));
  LED led_9 (.in(j_k_ff_9_q));

  // Notes on the sheet:
  //   Q0
  //   Q0
  //   Q1
  //   Q1
  //   Q2
  //   Q2
  //   Q0
  //   Q1
  //   Q2
endmodule
